// Digital circuit 1_Bit_ALU.dig as structural Verilog
module _1_Bit_ALU (
  input  a,
  input  b,
  input  Ainvert,
  input  Binvert,
  input  CarryIn,
  input  Less,
  input  [1:0] Operation,
  output Set,
  output CarryOut,
  output Result
);

  wire and_1_out, multiplexer_1_out, multiplexer_2_out, not_1_out, not_2_out, or_1_out;

  not not_1 (not_1_out, a);
  not not_2 (not_2_out, b);
  Multiplexer multiplexer_1 (.sel(Ainvert), .in_0(a), .in_1(not_1_out), .out(multiplexer_1_out));
  Multiplexer multiplexer_2 (.sel(Binvert), .in_0(b), .in_1(not_2_out), .out(multiplexer_2_out));
  and and_1 (and_1_out, multiplexer_1_out, multiplexer_2_out);
  or or_1 (or_1_out, multiplexer_1_out, multiplexer_2_out);
  _1_Bit_Full_Adder _1_bit_full_adder_1 (
    .a(multiplexer_1_out), .b(multiplexer_2_out), .CarryIn(CarryIn), .Set(Set), .CarryOut(CarryOut));
  Multiplexer #(.Selector_Bits(2)) multiplexer_3 (
    .sel(Operation), .in_0(and_1_out), .in_1(or_1_out), .in_2(Set), .in_3(Less), .out(Result));

  // Notes on the sheet:
  //   1-bit ALU
endmodule
