// Digital circuit 1_Bit_Full_Adder.dig as structural Verilog
module _1_Bit_Full_Adder (
  input  a,
  input  b,
  input  CarryIn,
  output Set,
  output CarryOut
);

  wire and_1_out, and_2_out, xor_1_out;

  xor xor_1 (xor_1_out, a, b);
  xor xor_2 (Set, xor_1_out, CarryIn);
  and and_1 (and_1_out, CarryIn, xor_1_out);
  and and_2 (and_2_out, a, b);
  or or_1 (CarryOut, and_1_out, and_2_out);

  // Notes on the sheet:
  //   1-bit full adder
endmodule
