// Digital circuit 1_Bit_Half_Adder.dig as structural Verilog
module _1_Bit_Half_Adder (
  input  A,
  input  B,
  output Sum,
  output Carry_out
);

  xor xor_1 (Sum, A, B);
  and and_1 (Carry_out, A, B);

  // Notes on the sheet:
  //   1-bit half-adder
endmodule
