// Digital circuit 8-bit ALU.dig as structural Verilog
module _8_bit_ALU (
  input  AInvert,
  input  BInvert,
  input  [1:0] Operation,
  input  [7:0] A,
  input  [7:0] B,
  output CarryOut,
  output [7:0] Result,
  output Set,
  output Set_2,
  output Set_3,
  output Set_4,
  output Set_5,
  output Set_6,
  output Set_7
);

  wire ALU0_carryout, ALU1_carryout, ALU2_carryout, ALU3_carryout, ALU4_carryout, ALU5_carryout,
       ALU6_carryout, ALU7_set;

  _1_Bit_ALU ALU0 (
    .a(A[0]), .b(B[0]), .Ainvert(AInvert), .Binvert(BInvert), .CarryIn(BInvert), .Less(ALU7_set),
    .Operation(Operation), .Set(Set), .CarryOut(ALU0_carryout), .Result(Result[0]));
  _1_Bit_ALU ALU1 (
    .a(A[1]), .b(B[1]), .Ainvert(AInvert), .Binvert(BInvert), .CarryIn(ALU0_carryout), .Less(1'b0),
    .Operation(Operation), .Set(Set_2), .CarryOut(ALU1_carryout), .Result(Result[1]));
  _1_Bit_ALU ALU2 (
    .a(A[2]), .b(B[2]), .Ainvert(AInvert), .Binvert(BInvert), .CarryIn(ALU1_carryout), .Less(1'b0),
    .Operation(Operation), .Set(Set_3), .CarryOut(ALU2_carryout), .Result(Result[2]));
  _1_Bit_ALU ALU3 (
    .a(A[3]), .b(B[3]), .Ainvert(AInvert), .Binvert(BInvert), .CarryIn(ALU2_carryout), .Less(1'b0),
    .Operation(Operation), .Set(Set_4), .CarryOut(ALU3_carryout), .Result(Result[3]));
  _1_Bit_ALU ALU4 (
    .a(A[4]), .b(B[4]), .Ainvert(AInvert), .Binvert(BInvert), .CarryIn(ALU3_carryout), .Less(1'b0),
    .Operation(Operation), .Set(Set_5), .CarryOut(ALU4_carryout), .Result(Result[4]));
  _1_Bit_ALU ALU5 (
    .a(A[5]), .b(B[5]), .Ainvert(AInvert), .Binvert(BInvert), .CarryIn(ALU4_carryout), .Less(1'b0),
    .Operation(Operation), .Set(Set_6), .CarryOut(ALU5_carryout), .Result(Result[5]));
  _1_Bit_ALU ALU6 (
    .a(A[6]), .b(B[6]), .Ainvert(AInvert), .Binvert(BInvert), .CarryIn(ALU5_carryout), .Less(1'b0),
    .Operation(Operation), .Set(Set_7), .CarryOut(ALU6_carryout), .Result(Result[6]));
  _1_Bit_ALU ALU7 (
    .a(A[7]), .b(B[7]), .Ainvert(AInvert), .Binvert(BInvert), .CarryIn(ALU6_carryout), .Less(1'b0),
    .Operation(Operation), .Set(ALU7_set), .CarryOut(CarryOut), .Result(Result[7]));

  // Notes on the sheet:
  //   8-bit ALU
endmodule
