// Digital circuit 256 x 8-bit Memory.dig as structural Verilog
module _256_x_8_bit_Memory (
  input  [31:0] Address,
  input  Write_Enable,
  input  [7:0] Write_Data,
  output [7:0] Read_Data
);

  wire _32_8bit_registerfile_1_p5, _32_8bit_registerfile_2_p5, _32_8bit_registerfile_3_p5,
       _32_8bit_registerfile_4_p5, _32_8bit_registerfile_5_p5, _32_8bit_registerfile_6_p5,
       _32_8bit_registerfile_7_p5, _32_8bit_registerfile_8_p5, and_1_out, and_2_out, and_3_out, and_4_out,
       and_5_out, and_6_out, and_7_out, and_8_out, decoder_1_out_0, decoder_1_out_1, decoder_1_out_2,
       decoder_1_out_3, decoder_1_out_4, decoder_1_out_5, decoder_1_out_6, decoder_1_out_7;

  Decoder #(.Selector_Bits(3)) decoder_1 (
    .sel(Address[7:5]), .out_0(decoder_1_out_0), .out_1(decoder_1_out_1), .out_2(decoder_1_out_2),
    .out_3(decoder_1_out_3), .out_4(decoder_1_out_4), .out_5(decoder_1_out_5), .out_6(decoder_1_out_6),
    .out_7(decoder_1_out_7));
  and and_1 (and_1_out, Write_Enable, decoder_1_out_0);
  and and_2 (and_2_out, Write_Enable, decoder_1_out_1);
  and and_3 (and_3_out, Write_Enable, decoder_1_out_2);
  and and_4 (and_4_out, Write_Enable, decoder_1_out_3);
  and and_5 (and_5_out, Write_Enable, decoder_1_out_4);
  and and_6 (and_6_out, Write_Enable, decoder_1_out_5);
  and and_7 (and_7_out, Write_Enable, decoder_1_out_6);
  and and_8 (and_8_out, Write_Enable, decoder_1_out_7);
  // _32_8Bit_RegisterFile _32_8bit_registerfile_1: pin names not known; wires that end beside it: Address[4:0], and_1_out, Address[4:0], Write_Data, _32_8bit_registerfile_1_p5
  // _32_8Bit_RegisterFile _32_8bit_registerfile_2: pin names not known; wires that end beside it: Address[4:0], and_2_out, Address[4:0], Write_Data, _32_8bit_registerfile_2_p5
  // _32_8Bit_RegisterFile _32_8bit_registerfile_3: pin names not known; wires that end beside it: Address[4:0], and_3_out, Address[4:0], Write_Data, _32_8bit_registerfile_3_p5
  // _32_8Bit_RegisterFile _32_8bit_registerfile_4: pin names not known; wires that end beside it: Address[4:0], and_4_out, Address[4:0], Write_Data, _32_8bit_registerfile_4_p5
  // _32_8Bit_RegisterFile _32_8bit_registerfile_5: pin names not known; wires that end beside it: Address[4:0], and_5_out, Address[4:0], Write_Data, _32_8bit_registerfile_5_p5
  // _32_8Bit_RegisterFile _32_8bit_registerfile_6: pin names not known; wires that end beside it: Address[4:0], and_6_out, Address[4:0], Write_Data, _32_8bit_registerfile_6_p5
  // _32_8Bit_RegisterFile _32_8bit_registerfile_7: pin names not known; wires that end beside it: Address[4:0], and_7_out, Address[4:0], Write_Data, _32_8bit_registerfile_7_p5
  // _32_8Bit_RegisterFile _32_8bit_registerfile_8: pin names not known; wires that end beside it: Address[4:0], and_8_out, Address[4:0], Write_Data, _32_8bit_registerfile_8_p5
  assign Read_Data[0] = decoder_1_out_0 ? _32_8bit_registerfile_1_p5 : 1'bz;  // Driver driver_1
  assign Read_Data[0] = decoder_1_out_1 ? _32_8bit_registerfile_2_p5 : 1'bz;  // Driver driver_2
  assign Read_Data[0] = decoder_1_out_2 ? _32_8bit_registerfile_3_p5 : 1'bz;  // Driver driver_3
  assign Read_Data[0] = decoder_1_out_3 ? _32_8bit_registerfile_4_p5 : 1'bz;  // Driver driver_4
  assign Read_Data[0] = decoder_1_out_4 ? _32_8bit_registerfile_5_p5 : 1'bz;  // Driver driver_5
  assign Read_Data[0] = decoder_1_out_5 ? _32_8bit_registerfile_6_p5 : 1'bz;  // Driver driver_6
  assign Read_Data[0] = decoder_1_out_6 ? _32_8bit_registerfile_7_p5 : 1'bz;  // Driver driver_7
  assign Read_Data[0] = decoder_1_out_7 ? _32_8bit_registerfile_8_p5 : 1'bz;  // Driver driver_8
  // Pins of 1 and 8 bits meet at Read_Data
endmodule
