// Digital circuit 8-bit ALU.dig as structural Verilog
module _8_bit_ALU (
  input  AInvert,
  input  BInvert,
  input  [1:0] Operation,
  input  [7:0] A,
  input  [7:0] B,
  output CarryOut,
  output [7:0] Result
);

  wire ALU0_carryout, ALU0_set, ALU1_carryout, ALU1_set, ALU2_carryout, ALU2_set, ALU3_carryout, ALU3_set,
       ALU4_carryout, ALU4_set, ALU5_carryout, ALU5_set, ALU6_carryout, ALU6_set, ALU7_set;

  _1_Bit_ALU ALU0 (
    .a(A[0]), .b(B[0]), .Ainvert(AInvert), .Binvert(BInvert), .CarryIn(BInvert), .Less(ALU7_set),
    .Operation(Operation), .Set(ALU0_set), .CarryOut(ALU0_carryout), .Result(Result[0]));
  _1_Bit_ALU ALU1 (
    .a(A[1]), .b(B[1]), .Ainvert(AInvert), .Binvert(BInvert), .CarryIn(ALU0_carryout), .Less(1'b0),
    .Operation(Operation), .Set(ALU1_set), .CarryOut(ALU1_carryout), .Result(Result[1]));
  _1_Bit_ALU ALU2 (
    .a(A[2]), .b(B[2]), .Ainvert(AInvert), .Binvert(BInvert), .CarryIn(ALU1_carryout), .Less(1'b0),
    .Operation(Operation), .Set(ALU2_set), .CarryOut(ALU2_carryout), .Result(Result[2]));
  _1_Bit_ALU ALU3 (
    .a(A[3]), .b(B[3]), .Ainvert(AInvert), .Binvert(BInvert), .CarryIn(ALU2_carryout), .Less(1'b0),
    .Operation(Operation), .Set(ALU3_set), .CarryOut(ALU3_carryout), .Result(Result[3]));
  _1_Bit_ALU ALU4 (
    .a(A[4]), .b(B[4]), .Ainvert(AInvert), .Binvert(BInvert), .CarryIn(ALU3_carryout), .Less(1'b0),
    .Operation(Operation), .Set(ALU4_set), .CarryOut(ALU4_carryout), .Result(Result[4]));
  _1_Bit_ALU ALU5 (
    .a(A[5]), .b(B[5]), .Ainvert(AInvert), .Binvert(BInvert), .CarryIn(ALU4_carryout), .Less(1'b0),
    .Operation(Operation), .Set(ALU5_set), .CarryOut(ALU5_carryout), .Result(Result[5]));
  _1_Bit_ALU ALU6 (
    .a(A[6]), .b(B[6]), .Ainvert(AInvert), .Binvert(BInvert), .CarryIn(ALU5_carryout), .Less(1'b0),
    .Operation(Operation), .Set(ALU6_set), .CarryOut(ALU6_carryout), .Result(Result[6]));
  _1_Bit_ALU ALU7 (
    .a(A[7]), .b(B[7]), .Ainvert(AInvert), .Binvert(BInvert), .CarryIn(ALU6_carryout), .Less(1'b0),
    .Operation(Operation), .Set(ALU7_set), .CarryOut(CarryOut), .Result(Result[7]));

  // Notes on the sheet:
  //   8-bit ALU
endmodule
