// Digital circuit 32-8Bit-RegisterFile.dig as structural Verilog
module _32_8Bit_RegisterFile (
  input  [4:0] Read_register_number_1,
  input  [4:0] Read_register_number_2,
  input  Write,
  input  [4:0] Write_Register,
  input  [7:0] Write_Data,
  output [7:0] Read_data_1,
  output [7:0] Read_data_2
);

  wire and_1_out, and_2_out, and_3_out, and_4_out, and_5_out, and_6_out, and_7_out, and_8_out, and_9_out,
       and_10_out, and_11_out, and_12_out, and_13_out, and_14_out, and_15_out, and_16_out, and_17_out,
       and_18_out, and_19_out, and_20_out, and_21_out, and_22_out, and_23_out, and_24_out, and_25_out,
       and_26_out, and_27_out, and_28_out, and_29_out, and_30_out, and_31_out, and_32_out, decoder_1_out_0,
       decoder_1_out_1, decoder_1_out_2, decoder_1_out_3, decoder_1_out_4, decoder_1_out_5, decoder_1_out_6,
       decoder_1_out_7, decoder_1_out_8, decoder_1_out_9, decoder_1_out_10, decoder_1_out_11,
       decoder_1_out_12, decoder_1_out_13, decoder_1_out_14, decoder_1_out_15, decoder_1_out_16,
       decoder_1_out_17, decoder_1_out_18, decoder_1_out_19, decoder_1_out_20, decoder_1_out_21,
       decoder_1_out_22, decoder_1_out_23, decoder_1_out_24, decoder_1_out_25, decoder_1_out_26,
       decoder_1_out_27, decoder_1_out_28, decoder_1_out_29, decoder_1_out_30, decoder_1_out_31;
  wire [7:0] X0_q, X1_q, X2_q, X3_q, X4_q, X5_q, X6_q, X7_q, X8_q, X9_q, X10_q, X11_q, X12_q, X13_q, X14_q,
       X15_q, X16_q, X17_q, X18_q, X19_q, X20_q, X21_q, X22_q, X23_q, X24_q, X25_q, X26_q, X27_q, X28_q,
       X29_q, X30_q, X31_q;

  Decoder #(.Selector_Bits(5)) decoder_1 (
    .sel(Write_Register), .out_0(decoder_1_out_0), .out_1(decoder_1_out_1), .out_2(decoder_1_out_2),
    .out_3(decoder_1_out_3), .out_4(decoder_1_out_4), .out_5(decoder_1_out_5), .out_6(decoder_1_out_6),
    .out_7(decoder_1_out_7), .out_8(decoder_1_out_8), .out_9(decoder_1_out_9), .out_10(decoder_1_out_10),
    .out_11(decoder_1_out_11), .out_12(decoder_1_out_12), .out_13(decoder_1_out_13),
    .out_14(decoder_1_out_14), .out_15(decoder_1_out_15), .out_16(decoder_1_out_16),
    .out_17(decoder_1_out_17), .out_18(decoder_1_out_18), .out_19(decoder_1_out_19),
    .out_20(decoder_1_out_20), .out_21(decoder_1_out_21), .out_22(decoder_1_out_22),
    .out_23(decoder_1_out_23), .out_24(decoder_1_out_24), .out_25(decoder_1_out_25),
    .out_26(decoder_1_out_26), .out_27(decoder_1_out_27), .out_28(decoder_1_out_28),
    .out_29(decoder_1_out_29), .out_30(decoder_1_out_30), .out_31(decoder_1_out_31));
  and and_1 (and_1_out, decoder_1_out_0, Write);
  and and_2 (and_2_out, decoder_1_out_1, Write);
  and and_3 (and_3_out, decoder_1_out_2, Write);
  and and_4 (and_4_out, decoder_1_out_3, Write);
  and and_5 (and_5_out, decoder_1_out_4, Write);
  and and_6 (and_6_out, decoder_1_out_5, Write);
  and and_7 (and_7_out, decoder_1_out_6, Write);
  and and_8 (and_8_out, decoder_1_out_7, Write);
  and and_9 (and_9_out, decoder_1_out_8, Write);
  and and_10 (and_10_out, decoder_1_out_9, Write);
  and and_11 (and_11_out, decoder_1_out_10, Write);
  and and_12 (and_12_out, decoder_1_out_11, Write);
  and and_13 (and_13_out, decoder_1_out_12, Write);
  and and_14 (and_14_out, decoder_1_out_13, Write);
  and and_15 (and_15_out, decoder_1_out_14, Write);
  and and_16 (and_16_out, decoder_1_out_15, Write);
  and and_17 (and_17_out, decoder_1_out_16, Write);
  and and_18 (and_18_out, decoder_1_out_17, Write);
  and and_19 (and_19_out, decoder_1_out_18, Write);
  and and_20 (and_20_out, decoder_1_out_19, Write);
  and and_21 (and_21_out, decoder_1_out_20, Write);
  and and_22 (and_22_out, decoder_1_out_21, Write);
  and and_23 (and_23_out, decoder_1_out_22, Write);
  and and_24 (and_24_out, decoder_1_out_23, Write);
  and and_25 (and_25_out, decoder_1_out_24, Write);
  and and_26 (and_26_out, decoder_1_out_25, Write);
  and and_27 (and_27_out, decoder_1_out_26, Write);
  and and_28 (and_28_out, decoder_1_out_27, Write);
  and and_29 (and_29_out, decoder_1_out_28, Write);
  and and_30 (and_30_out, decoder_1_out_29, Write);
  and and_31 (and_31_out, decoder_1_out_30, Write);
  and and_32 (and_32_out, decoder_1_out_31, Write);
  D_FF #(.Bits(8)) X0 (.D(Write_Data), .C(and_1_out), .Q(X0_q));  // open: nQ
  D_FF #(.Bits(8)) X1 (.D(Write_Data), .C(and_2_out), .Q(X1_q));  // open: nQ
  D_FF #(.Bits(8)) X2 (.D(Write_Data), .C(and_3_out), .Q(X2_q));  // open: nQ
  D_FF #(.Bits(8)) X3 (.D(Write_Data), .C(and_4_out), .Q(X3_q));  // open: nQ
  D_FF #(.Bits(8)) X4 (.D(Write_Data), .C(and_5_out), .Q(X4_q));  // open: nQ
  D_FF #(.Bits(8)) X5 (.D(Write_Data), .C(and_6_out), .Q(X5_q));  // open: nQ
  D_FF #(.Bits(8)) X6 (.D(Write_Data), .C(and_7_out), .Q(X6_q));  // open: nQ
  D_FF #(.Bits(8)) X7 (.D(Write_Data), .C(and_8_out), .Q(X7_q));  // open: nQ
  D_FF #(.Bits(8)) X8 (.D(Write_Data), .C(and_9_out), .Q(X8_q));  // open: nQ
  D_FF #(.Bits(8)) X9 (.D(Write_Data), .C(and_10_out), .Q(X9_q));  // open: nQ
  D_FF #(.Bits(8)) X10 (.D(Write_Data), .C(and_11_out), .Q(X10_q));  // open: nQ
  D_FF #(.Bits(8)) X11 (.D(Write_Data), .C(and_12_out), .Q(X11_q));  // open: nQ
  D_FF #(.Bits(8)) X12 (.D(Write_Data), .C(and_13_out), .Q(X12_q));  // open: nQ
  D_FF #(.Bits(8)) X13 (.D(Write_Data), .C(and_14_out), .Q(X13_q));  // open: nQ
  D_FF #(.Bits(8)) X14 (.D(Write_Data), .C(and_15_out), .Q(X14_q));  // open: nQ
  D_FF #(.Bits(8)) X15 (.D(Write_Data), .C(and_16_out), .Q(X15_q));  // open: nQ
  D_FF #(.Bits(8)) X16 (.D(Write_Data), .C(and_17_out), .Q(X16_q));  // open: nQ
  D_FF #(.Bits(8)) X17 (.D(Write_Data), .C(and_18_out), .Q(X17_q));  // open: nQ
  D_FF #(.Bits(8)) X18 (.D(Write_Data), .C(and_19_out), .Q(X18_q));  // open: nQ
  D_FF #(.Bits(8)) X19 (.D(Write_Data), .C(and_20_out), .Q(X19_q));  // open: nQ
  D_FF #(.Bits(8)) X20 (.D(Write_Data), .C(and_21_out), .Q(X20_q));  // open: nQ
  D_FF #(.Bits(8)) X21 (.D(Write_Data), .C(and_22_out), .Q(X21_q));  // open: nQ
  D_FF #(.Bits(8)) X22 (.D(Write_Data), .C(and_23_out), .Q(X22_q));  // open: nQ
  D_FF #(.Bits(8)) X23 (.D(Write_Data), .C(and_24_out), .Q(X23_q));  // open: nQ
  D_FF #(.Bits(8)) X24 (.D(Write_Data), .C(and_25_out), .Q(X24_q));  // open: nQ
  D_FF #(.Bits(8)) X25 (.D(Write_Data), .C(and_26_out), .Q(X25_q));  // open: nQ
  D_FF #(.Bits(8)) X26 (.D(Write_Data), .C(and_27_out), .Q(X26_q));  // open: nQ
  D_FF #(.Bits(8)) X27 (.D(Write_Data), .C(and_28_out), .Q(X27_q));  // open: nQ
  D_FF #(.Bits(8)) X28 (.D(Write_Data), .C(and_29_out), .Q(X28_q));  // open: nQ
  D_FF #(.Bits(8)) X29 (.D(Write_Data), .C(and_30_out), .Q(X29_q));  // open: nQ
  D_FF #(.Bits(8)) X30 (.D(Write_Data), .C(and_31_out), .Q(X30_q));  // open: nQ
  D_FF #(.Bits(8)) X31 (.D(Write_Data), .C(and_32_out), .Q(X31_q));  // open: nQ
  Multiplexer #(.Selector_Bits(5), .Bits(8)) multiplexer_1 (
    .sel(Read_register_number_1), .in_0(X0_q), .in_1(X1_q), .in_2(X2_q), .in_3(X3_q), .in_4(X4_q),
    .in_5(X5_q), .in_6(X6_q), .in_7(X7_q), .in_8(X8_q), .in_9(X9_q), .in_10(X10_q), .in_11(X11_q),
    .in_12(X12_q), .in_13(X13_q), .in_14(X14_q), .in_15(X15_q), .in_16(X16_q), .in_17(X17_q), .in_18(X18_q),
    .in_19(X19_q), .in_20(X20_q), .in_21(X21_q), .in_22(X22_q), .in_23(X23_q), .in_24(X24_q), .in_25(X25_q),
    .in_26(X26_q), .in_27(X27_q), .in_28(X28_q), .in_29(X29_q), .in_30(X30_q), .in_31(X31_q),
    .out(Read_data_1));
  Multiplexer #(.Selector_Bits(5), .Bits(8)) multiplexer_2 (
    .sel(Read_register_number_2), .in_0(X0_q), .in_1(X1_q), .in_2(X2_q), .in_3(X3_q), .in_4(X4_q),
    .in_5(X5_q), .in_6(X6_q), .in_7(X7_q), .in_8(X8_q), .in_9(X9_q), .in_10(X10_q), .in_11(X11_q),
    .in_12(X12_q), .in_13(X13_q), .in_14(X14_q), .in_15(X15_q), .in_16(X16_q), .in_17(X17_q), .in_18(X18_q),
    .in_19(X19_q), .in_20(X20_q), .in_21(X21_q), .in_22(X22_q), .in_23(X23_q), .in_24(X24_q), .in_25(X25_q),
    .in_26(X26_q), .in_27(X27_q), .in_28(X28_q), .in_29(X29_q), .in_30(X30_q), .in_31(X31_q),
    .out(Read_data_2));
endmodule
