// Digital circuit 32-1-mux.dig as structural Verilog
module _32_1_mux (
  input  [4:0] X0,
  input  [4:0] X1,
  input  [4:0] X2,
  input  [4:0] X3,
  input  [4:0] X4,
  input  [4:0] X5,
  input  [4:0] X6,
  input  [4:0] X7,
  input  [4:0] X8,
  input  [4:0] X9,
  input  [4:0] X10,
  input  [4:0] X11,
  input  [4:0] X12,
  input  [4:0] X13,
  input  [4:0] X14,
  input  [4:0] X15,
  input  [4:0] X16,
  input  [4:0] X17,
  input  [4:0] X18,
  input  [4:0] X19,
  input  [4:0] X20,
  input  [4:0] X21,
  input  [4:0] X22,
  input  [4:0] X23,
  input  [4:0] X24,
  input  [4:0] X25,
  input  [4:0] X26,
  input  [4:0] X27,
  input  [4:0] X28,
  input  [4:0] X29,
  input  [4:0] X30,
  input  [4:0] X31,
  input  [4:0] RS1,
  output [4:0] RS1_2
);

  Multiplexer #(.Bits(5), .Selector_Bits(5)) multiplexer_1 (
    .sel(RS1), .in_0(X0), .in_1(X1), .in_2(X2), .in_3(X3), .in_4(X4), .in_5(X5), .in_6(X6), .in_7(X7),
    .in_8(X8), .in_9(X9), .in_10(X10), .in_11(X11), .in_12(X12), .in_13(X13), .in_14(X14), .in_15(X15),
    .in_16(X16), .in_17(X17), .in_18(X18), .in_19(X19), .in_20(X20), .in_21(X21), .in_22(X22), .in_23(X23),
    .in_24(X24), .in_25(X25), .in_26(X26), .in_27(X27), .in_28(X28), .in_29(X29), .in_30(X30), .in_31(X31),
    .out(RS1_2));

  // Notes on the sheet:
  //   Task #3
endmodule
