// Digital circuit 5-32-decoder.dig as structural Verilog
module _5_32_decoder (
  input  [4:0] RD,
  output WE15,
  output WE14,
  output WE13,
  output WE12,
  output WE11,
  output WE10,
  output WE9,
  output WE8,
  output WE7,
  output WE6,
  output WE5,
  output WE4,
  output WE3,
  output WE2,
  output WE1,
  output WE0,
  output WE16,
  output WE17,
  output WE18,
  output WE19,
  output WE20,
  output WE21,
  output WE22,
  output WE23,
  output WE24,
  output WE25,
  output WE26,
  output WE27,
  output WE28,
  output WE29,
  output WE30,
  output WE31
);

  Decoder #(.Selector_Bits(5)) decoder_1 (
    .sel(RD), .out_0(WE0), .out_1(WE1), .out_2(WE2), .out_3(WE3), .out_4(WE4), .out_5(WE5), .out_6(WE6),
    .out_7(WE7), .out_8(WE8), .out_9(WE9), .out_10(WE10), .out_11(WE11), .out_12(WE12), .out_13(WE13),
    .out_14(WE14), .out_15(WE15), .out_16(WE16), .out_17(WE17), .out_18(WE18), .out_19(WE19), .out_20(WE20),
    .out_21(WE21), .out_22(WE22), .out_23(WE23), .out_24(WE24), .out_25(WE25), .out_26(WE26), .out_27(WE27),
    .out_28(WE28), .out_29(WE29), .out_30(WE30), .out_31(WE31));

  // Notes on the sheet:
  //   Task #5
endmodule
