// Digital circuit Lab-07-Task-2.dig as structural Verilog
module Lab_07_Task_2 (
  input  Input_A,
  input  Input_B,
  input  Input_S,
  output Output_C
);

  wire and_1_out, and_2_out, not_1_out;

  not not_1 (not_1_out, Input_S);
  and and_1 (and_1_out, Input_A, not_1_out);
  and and_2 (and_2_out, Input_S, Input_B);
  or or_1 (Output_C, and_1_out, and_2_out);

  // Notes on the sheet:
  //   Task #2
endmodule
