// Digital circuit Lab-07-Task-4.dig as structural Verilog
module Lab_07_Task_4 (
  input  Input_A,
  input  Input_B,
  input  Input_C,
  output Output_0,
  output Output_1,
  output Output_2,
  output Output_3,
  output Output_4,
  output Output_5,
  output Output_6,
  output Output_7
);

  wire not_1_out, not_2_out, not_3_out;

  not not_1 (not_1_out, Input_A);
  not not_2 (not_2_out, Input_B);
  not not_3 (not_3_out, Input_C);
  and and_1 (Output_0, not_1_out, not_2_out, not_3_out);
  and and_2 (Output_1, Input_A, not_2_out, not_3_out);
  and and_3 (Output_2, not_1_out, Input_B, not_3_out);
  and and_4 (Output_3, Input_A, Input_B, not_3_out);
  and and_5 (Output_4, not_1_out, not_2_out, Input_C);
  and and_6 (Output_5, Input_A, not_2_out, Input_C);
  and and_7 (Output_6, not_1_out, Input_B, Input_C);
  and and_8 (Output_7, Input_A, Input_B, Input_C);

  // Notes on the sheet:
  //   Task #4
endmodule
