// Digital circuit SingleCycleCPU.dig as structural Verilog
module SingleCycleCPU (
  input  [3:0] _4
);

  wire _8_bit_alu_1_p1, _8_bit_alu_1_p4, _32_8bit_registerfile_1_p6, and_1_out, control_1_p2, control_1_p3,
       control_1_p4, control_1_p5, control_1_p6, control_1_p7, control_1_p8, pc_1_p2, shift_left_1_1_p2;
  wire [6:0] alu_control_1_p2;
  wire [31:0] _8_bit_alu_1_p5, _32_8bit_registerfile_1_p5, _32_8bit_registerfile_1_p7, adder_1_p3,
       adder_2_p3, Data_Memory_p4, imm_gen_1_p2, Instruction_Memory_p2, multiplexer_1_out, pc_1_p1;

  // PC pc_1: pin names not known; wires that end beside it: pc_1_p1, pc_1_p2
  // Adder adder_1: pin names not known; wires that end beside it: pc_1_p2, _4, adder_1_p3
  // _256_x_8_bit_Memory Instruction_Memory: pin names not known; wires that end beside it: pc_1_p2, Instruction_Memory_p2
  // Control control_1: pin names not known; wires that end beside it: Instruction_Memory_p2[6:0], control_1_p2, control_1_p3, control_1_p4, control_1_p5, control_1_p6, control_1_p7, control_1_p8, control_1_p4
  // _32_8Bit_RegisterFile _32_8bit_registerfile_1: pin names not known; wires that end beside it: Instruction_Memory_p2[19:15], Instruction_Memory_p2[24:20], control_1_p8, Instruction_Memory_p2[11:7], _32_8bit_registerfile_1_p5, _32_8bit_registerfile_1_p6, _32_8bit_registerfile_1_p7
  // Imm_Gen imm_gen_1: pin names not known; wires that end beside it: Instruction_Memory_p2, imm_gen_1_p2
  // Shift_left_1 shift_left_1_1: pin names not known; wires that end beside it: imm_gen_1_p2, shift_left_1_1_p2
  Multiplexer #(.Bits(32)) multiplexer_1 (
    .sel(control_1_p7), .in_0(_32_8bit_registerfile_1_p7), .in_1(imm_gen_1_p2), .out(multiplexer_1_out));
  // _8_bit_ALU _8_bit_alu_1: pin names not known; wires that end beside it: _8_bit_alu_1_p1, _32_8bit_registerfile_1_p6, multiplexer_1_out, _8_bit_alu_1_p4, _8_bit_alu_1_p5
  // ALU_Control alu_control_1: pin names not known; wires that end beside it: control_1_p2, alu_control_1_p2, _8_bit_alu_1_p1
  // Adder adder_2: pin names not known; wires that end beside it: pc_1_p2, shift_left_1_1_p2, adder_2_p3
  // _256_x_8_bit_Memory Data_Memory: pin names not known; wires that end beside it: _8_bit_alu_1_p5, control_1_p6, _32_8bit_registerfile_1_p7, Data_Memory_p4
  and and_1 (and_1_out, control_1_p5, _8_bit_alu_1_p4);
  Multiplexer #(.Bits(32)) multiplexer_2 (
    .sel(control_1_p3), .in_0(_8_bit_alu_1_p5), .in_1(Data_Memory_p4), .out(_32_8bit_registerfile_1_p5));
  Multiplexer #(.Bits(32)) multiplexer_3 (.sel(and_1_out), .in_0(adder_1_p3), .in_1(adder_2_p3), .out(pc_1_p1));
endmodule
