// Digital circuit Lab-07-Task-1.dig as structural Verilog
module Lab_07_Task_1 (
  input  Input_A,
  input  Input_B,
  input  Input_C,
  output Output_Y
);

  wire and_1_out, and_2_out, not_1_out, not_2_out;

  not not_1 (not_1_out, Input_A);
  not not_2 (not_2_out, Input_B);
  and and_1 (and_1_out, not_1_out, not_2_out, Input_C);
  and and_2 (and_2_out, Input_B, Input_A);
  or or_1 (Output_Y, and_1_out, and_2_out);

  // Notes on the sheet:
  //   Task #1
  //   A'B'C
  //   AB
  //   Y = A'B'C + AB
endmodule
